# Fritzing sketch Girassol (saved by Fritzing 0.9.2b)
breadboards: 1

parts:
  Componente1 = Arduino Uno (Rev3)
  Resistor = Resistor [tolerance=±5% resistance=1k package=THT]
  LDR = Photocell (LDR) [package=THT]
  LDR1 = Photocell (LDR) [package=THT]
  Resistor1 = Resistor [tolerance=±5% resistance=1k package=THT]
  MOTOR1 = 28BYJ-48 Stepper Motor
  BREAKOUT1 = ULN2003A breakout board

nets (from the breadboard view):
  N1: Componente1.A0, LDR1.pin_1, Resistor1.Pin_0
  N2: Componente1.A1, Resistor.Pin_0, LDR.pin_1
  N3: Componente1.D8, BREAKOUT1.In_1
  N4: Componente1.D9_PWM, BREAKOUT1.In_2
  N5: Componente1.D10_PWM/SS, BREAKOUT1.In_3
  N6: Componente1.D11_PWM/MOSI, BREAKOUT1.In_4
  N7: Componente1.GND, Resistor.Pin_1, Resistor1.Pin_1, BREAKOUT1.0V
  5V: Componente1.5V, LDR.pin_0, LDR1.pin_0, BREAKOUT1.+5V
  N8: MOTOR1.RED, BREAKOUT1.RED_wire
  N9: MOTOR1.ORANGE, BREAKOUT1.ORANGE_wire
  N10: MOTOR1.YELLOW, BREAKOUT1.YELLOW_wire
  N11: MOTOR1.PINK, BREAKOUT1.PINK_wire
  N12: MOTOR1.BLUE, BREAKOUT1.BLUE_wire

notes:
  A1 e A0
  8~11

custom parts:
  ULN2003A breakout board: ULN2003A 7-way Darlington Transistor Driver on breakoutboard
